# Fritzing sketch esp-generic-board (saved by Fritzing 0.9.10b)
circuit board: 6cm x 8cm
breadboards: 1

parts:
  GND = Camdenboss CTB0158-3 [part_number=CTB0158-3 package=THT]
  3V3 = Camdenboss CTB0158-3 [part_number=CTB0158-3 package=THT]
  5V = Camdenboss CTB0158-3 [part_number=CTB0158-3 package=THT]
  UART = male pin header, 2 pins [form="♂ (male)"]
  V3_3 = Header 2 [package=jst-2-pth]
  V5_0 = Header 2 [package=jst-2-pth]
  27 = Resistor [tolerance=±5% resistance=0 power=0.25 package=THT]
  26 = Resistor [tolerance=±5% resistance=0 power=0.25 package=THT]
  25 = Resistor [tolerance=±5% resistance=0 power=0.25 package=THT]
  33 = Resistor [tolerance=±5% resistance=0 power=0.25 package=THT]
  32 = Resistor [tolerance=±5% resistance=0 power=0.25 package=THT]
  23 = Resistor [tolerance=±5% resistance=0 power=0.25 package=THT]
  I2CB = male pin header, 4 pins [form="♂ (male)"]
  I2C = male pin header, 4 pins [form="♂ (male)"]
  GPIO1 = male pin header, 4 pins [form="♂ (male)"]
  Jin = male pin header, 3 pins [form="♂ (male)"]
  AC = Camdenboss CTB0158-2 [part_number=CTB0158-2 package=THT]
  GPIO3 = male pin header, 4 pins [form="♂ (male)"]
  GPIO4 = male pin header, 4 pins [form="♂ (male)"]
  Jout = male pin header, 3 pins [form="♂ (male)"]
  GPIO2 = male pin header, 4 pins [form="♂ (male)"]
  HLK-PM1 = HLK-PM01
  U1 = ESP32-38PinWide [part_number=ESP32-38PinWide]

nets:
  GND: GND.pin1, GND.pin2, GND.pin3, V3_3.2, V5_0.2, I2CB.pin1, I2C.pin1, GPIO1.pin1, GPIO3.pin1, GPIO4.pin1, GPIO2.pin1, HLK-PM1.-Vo, U1.GND
  N1: 3V3.pin1, 3V3.pin2, 3V3.pin3, V3_3.1, I2CB.pin4, I2C.pin4, GPIO1.pin4, Jin.pin3, Jout.pin3, U1.3.3
  N2: 5V.pin1, 5V.pin2, 5V.pin3, V5_0.1, Jin.pin1, Jout.pin1, U1.VIN
  N3: UART.pin1, U1.GPIO1
  N4: UART.pin2, U1.GPIO3
  N5: 27.Pin_0, GPIO2.pin3
  N6: 27.Pin_1, U1.GPIO27
  N7: 26.Pin_0, GPIO4.pin2
  N8: 26.Pin_1, U1.GPIO26
  N9: 25.Pin_0, GPIO4.pin3
  N10: 25.Pin_1, U1.GPIO25
  N11: 33.Pin_0, GPIO3.pin2
  N12: 33.Pin_1, U1.GPIO33
  N13: 32.Pin_0, GPIO3.pin3
  N14: 32.Pin_1, U1.GPIO32
  N15: 23.Pin_0, GPIO2.pin2
  N16: 23.Pin_1, U1.GPIO23
  N17: I2CB.pin2, U1.GPIO17
  N18: I2CB.pin3, U1.GPIO16
  N19: I2C.pin2, U1.GPIO22
  N20: I2C.pin3, U1.GPIO21
  N21: GPIO1.pin2, U1.GPIO19
  N22: GPIO1.pin3, U1.GPIO18
  N23: Jin.pin2, HLK-PM1.+Vo
  N24: AC.pin1, HLK-PM1.AC#0
  N25: AC.pin2, HLK-PM1.AC#1
  N26: GPIO3.pin4, GPIO4.pin4, Jout.pin2, GPIO2.pin4

notes:
  Simon
  EGB
  2.0.0
  5.0V
  3.3V

custom parts:
  HLK-PM01: AC-DC 220V to 5V Step-Down Power Supply Module
  ESP32-38PinWide: Generic 38-Pin ESP32 with wide format (only access to one side of pins on a breadboard) based on Stephen Lilley's HiLetgo ESP-WROOM-32 ESP32 ESP-32S Development Board.
